# Fritzing sketch pushbutton (saved by Fritzing 0.8.5b)
breadboards: 1

parts:
  Raspberry_Pi_B_rev1 = Raspberry Pi B rev2
  Pulldown = Resistor [tolerance=±5% resistance=1k package=THT]
  R3 = Resistor [tolerance=±5% resistance=2.2k package=THT]
  S2 = Pushbutton [package=THT]

nets:
  N1: Raspberry_Pi_B_rev1.3V3, S2.leg1
  N2: Raspberry_Pi_B_rev1.GND, Pulldown.Pin_1
  N3: Raspberry_Pi_B_rev1.GPIO_7, R3.Pin_1
  N4: Pulldown.Pin_0, R3.Pin_0, S2.leg0
